// Logisim project Output.circ as structural Verilog: 3 circuits, main circuit Output to Screen
module Output_to_Screen (
  input  [15:0] in_1
);

  wire [3:0] hex_to_decimal_plaecs_1__1, hex_to_decimal_plaecs_1__1_000, hex_to_decimal_plaecs_1__10,
       hex_to_decimal_plaecs_1__10_000, hex_to_decimal_plaecs_1__100;
  wire [7:0] hex_to_7_1_output, hex_to_7_2_output, hex_to_7_3_output, hex_to_7_4_output, hex_to_7_5_output;

  _7_Segment_Display u_7_segment_display_1 (
    .g(hex_to_7_1_output[4]), .f(hex_to_7_1_output[5]), .a(hex_to_7_1_output[6]), .b(hex_to_7_1_output[7]),
    .e(hex_to_7_1_output[3]), .d(hex_to_7_1_output[2]), .c(hex_to_7_1_output[1]), .dp(hex_to_7_1_output[0]));
  hex_to_7 hex_to_7_1 (.INPUT(hex_to_decimal_plaecs_1__10_000), .Output(hex_to_7_1_output));
  _7_Segment_Display u_7_segment_display_2 (
    .g(hex_to_7_2_output[4]), .f(hex_to_7_2_output[5]), .a(hex_to_7_2_output[6]), .b(hex_to_7_2_output[7]),
    .e(hex_to_7_2_output[3]), .d(hex_to_7_2_output[2]), .c(hex_to_7_2_output[1]), .dp(hex_to_7_2_output[0]));
  hex_to_7 hex_to_7_2 (.INPUT(hex_to_decimal_plaecs_1__1_000), .Output(hex_to_7_2_output));
  _7_Segment_Display u_7_segment_display_3 (
    .g(hex_to_7_3_output[4]), .f(hex_to_7_3_output[5]), .a(hex_to_7_3_output[6]), .b(hex_to_7_3_output[7]),
    .e(hex_to_7_3_output[3]), .d(hex_to_7_3_output[2]), .c(hex_to_7_3_output[1]), .dp(hex_to_7_3_output[0]));
  hex_to_7 hex_to_7_3 (.INPUT(hex_to_decimal_plaecs_1__100), .Output(hex_to_7_3_output));
  hex_to_decimal_plaecs hex_to_decimal_plaecs_1 (
    .Input(in_1), ._10_000(hex_to_decimal_plaecs_1__10_000), ._1_000(hex_to_decimal_plaecs_1__1_000),
    ._100(hex_to_decimal_plaecs_1__100), ._10(hex_to_decimal_plaecs_1__10), ._1(hex_to_decimal_plaecs_1__1));
  _7_Segment_Display u_7_segment_display_4 (
    .g(hex_to_7_4_output[4]), .f(hex_to_7_4_output[5]), .a(hex_to_7_4_output[6]), .b(hex_to_7_4_output[7]),
    .e(hex_to_7_4_output[3]), .d(hex_to_7_4_output[2]), .c(hex_to_7_4_output[1]), .dp(hex_to_7_4_output[0]));
  hex_to_7 hex_to_7_4 (.INPUT(hex_to_decimal_plaecs_1__10), .Output(hex_to_7_4_output));
  _7_Segment_Display u_7_segment_display_5 (
    .g(hex_to_7_5_output[4]), .f(hex_to_7_5_output[5]), .a(hex_to_7_5_output[6]), .b(hex_to_7_5_output[7]),
    .e(hex_to_7_5_output[3]), .d(hex_to_7_5_output[2]), .c(hex_to_7_5_output[1]), .dp(hex_to_7_5_output[0]));
  hex_to_7 hex_to_7_5 (.INPUT(hex_to_decimal_plaecs_1__1), .Output(hex_to_7_5_output));
endmodule

module hex_to_7 (
  input  [3:0] INPUT,
  output [7:0] Output
);

  Multiplexer #(.select(4), .enable("false")) multiplexer_1 (
    .in0(1'b1), .in1(1'b0), .in2(1'b1), .in3(1'b1), .in4(1'b0), .in5(1'b1), .in6(1'b1), .in7(1'b1),
    .in8(1'b1), .in9(1'b1), .out(Output[6]), .sel(INPUT));  // open: in10, in11, in12, in13, in14, in15
  Multiplexer #(.select(4), .enable("false")) multiplexer_2 (
    .in0(1'b1), .in1(1'b1), .in2(1'b1), .in3(1'b1), .in4(1'b1), .in5(1'b0), .in6(1'b0), .in7(1'b1),
    .in8(1'b1), .in9(1'b1), .out(Output[7]), .sel(INPUT));  // open: in10, in11, in12, in13, in14, in15
  Multiplexer #(.select(4), .enable("false")) multiplexer_3 (
    .in0(1'b1), .in1(1'b1), .in2(1'b0), .in3(1'b1), .in4(1'b1), .in5(1'b1), .in6(1'b1), .in7(1'b1),
    .in8(1'b1), .in9(1'b1), .out(Output[1]), .sel(INPUT));  // open: in10, in11, in12, in13, in14, in15
  Multiplexer #(.select(4), .enable("false")) multiplexer_4 (
    .in0(1'b1), .in1(1'b0), .in2(1'b1), .in3(1'b1), .in4(1'b0), .in5(1'b1), .in6(1'b1), .in7(1'b0),
    .in8(1'b1), .in9(1'b1), .out(Output[2]), .sel(INPUT));  // open: in10, in11, in12, in13, in14, in15
  Multiplexer #(.select(4), .enable("false")) multiplexer_5 (
    .in0(1'b1), .in1(1'b0), .in2(1'b1), .in3(1'b0), .in4(1'b0), .in5(1'b0), .in6(1'b1), .in7(1'b0),
    .in8(1'b1), .in9(1'b0), .out(Output[3]), .sel(INPUT));  // open: in10, in11, in12, in13, in14, in15
  Multiplexer #(.select(4), .enable("false")) multiplexer_6 (
    .in0(1'b1), .in1(1'b0), .in2(1'b0), .in3(1'b0), .in4(1'b1), .in5(1'b1), .in6(1'b1), .in7(1'b0),
    .in8(1'b1), .in9(1'b1), .out(Output[5]), .sel(INPUT));  // open: in10, in11, in12, in13, in14, in15
  Multiplexer #(.select(4), .enable("false")) multiplexer_7 (
    .in0(1'b0), .in1(1'b0), .in2(1'b1), .in3(1'b1), .in4(1'b1), .in5(1'b1), .in6(1'b1), .in7(1'b0),
    .in8(1'b1), .in9(1'b1), .out(Output[4]), .sel(INPUT));  // open: in10, in11, in12, in13, in14, in15

  // Notes on the sheet:
  //   A
  //   B
  //   C
  //   D
  //   E
  //   F
  //   G
endmodule

module hex_to_decimal_plaecs (
  input  [15:0] Input,
  output [3:0] _10_000,
  output [3:0] _1_000,
  output [3:0] _100,
  output [3:0] _10,
  output [3:0] _1
);

  wire [3:0] divider_1_out, divider_1_out_2, divider_2_out, divider_2_out_2, divider_2_out_3, divider_3_out,
       divider_3_out_2, divider_3_out_3, divider_4_out, divider_4_out_2, divider_4_out_3, divider_4_rem,
       divider_4_rem_2, divider_4_rem_3;
  wire [15:0] divider_1_rem, divider_2_rem, divider_3_rem;
  wire [15:12] divider_1_out_3;

  Divider #(.width(16)) divider_1 (
    .a(Input), .b(16'h2710), .out({divider_1_out_3, divider_1_out_2, divider_1_out, _10_000}),
    .rem(divider_1_rem));  // open: upper
  Divider #(.width(16)) divider_2 (
    .a(divider_1_rem), .b(16'h3e8), .out({divider_2_out_3, divider_2_out_2, divider_2_out, _1_000}),
    .rem(divider_2_rem));  // open: upper
  Divider #(.width(16)) divider_3 (
    .a(divider_2_rem), .b(16'h64), .out({divider_3_out_3, divider_3_out_2, divider_3_out, _100}),
    .rem(divider_3_rem));  // open: upper
  Divider #(.width(16)) divider_4 (
    .a(divider_3_rem), .b(16'ha), .out({divider_4_out_3, divider_4_out_2, divider_4_out, _10}),
    .rem({divider_4_rem_3, divider_4_rem_2, divider_4_rem, _1}));  // open: upper
endmodule
