// Logisim project cpu 1.2.circ as structural Verilog: 12 circuits, main circuit main
module _16_register_file (
  input  [15:0] d,
  input  Clk,
  input  [3:0] Rd,
  input  Clr,
  input  [3:0] Ra,
  input  [3:0] Rb,
  output [15:0] a,
  output [15:0] b
);

  wire demultiplexer_1_out0, demultiplexer_1_out1, demultiplexer_1_out2, demultiplexer_1_out3;
  wire [15:0] four_register_file_1_a, four_register_file_1_b, four_register_file_2_a, four_register_file_2_b,
       four_register_file_3_a, four_register_file_3_b, three_register_file_1_a, three_register_file_1_b;

  Demultiplexer #(.select(2), .enable("false")) demultiplexer_1 (
    .out0(demultiplexer_1_out0), .out1(demultiplexer_1_out1), .out2(demultiplexer_1_out2),
    .out3(demultiplexer_1_out3), .in(Clk), .sel(Rd[3:2]));
  three_register_file three_register_file_1 (
    .d(d), .Ck(demultiplexer_1_out0), .Rd(Rd[1:0]), .Clr(Clr), .Ra(Ra[1:0]), .Rb(Rb[1:0]),
    .a(three_register_file_1_a), .b(three_register_file_1_b));
  four_register_file four_register_file_1 (
    .d(d), .Ck(demultiplexer_1_out1), .Rd(Rd[1:0]), .Clr(Clr), .Ra(Ra[1:0]), .Rb(Rb[1:0]),
    .a(four_register_file_1_a), .b(four_register_file_1_b));
  four_register_file four_register_file_2 (
    .d(d), .Ck(demultiplexer_1_out2), .Rd(Rd[1:0]), .Clr(Clr), .Ra(Ra[1:0]), .Rb(Rb[1:0]),
    .a(four_register_file_2_a), .b(four_register_file_2_b));
  four_register_file four_register_file_3 (
    .d(d), .Ck(demultiplexer_1_out3), .Rd(Rd[1:0]), .Clr(Clr), .Ra(Ra[1:0]), .Rb(Rb[1:0]),
    .a(four_register_file_3_a), .b(four_register_file_3_b));
  Multiplexer #(.select(2), .width(16), .enable("false")) multiplexer_1 (
    .in0(three_register_file_1_a), .in1(four_register_file_1_a), .in2(four_register_file_2_a),
    .in3(four_register_file_3_a), .out(a), .sel(Ra[3:2]));
  Multiplexer #(.select(2), .width(16), .enable("false")) multiplexer_2 (
    .in0(three_register_file_1_b), .in1(four_register_file_1_b), .in2(four_register_file_2_b),
    .in3(four_register_file_3_b), .out(b), .sel(Rb[3:2]));
endmodule

module main (
  input  in_1,
  input  Reset
);

  wire and_1_out, and_2_out, bus_control_1_alu_enable, bus_control_1_bus_read, bus_control_1_bus_write,
       bus_control_1_display_ready, bus_control_1_read_enabled, bus_control_1_reg_write, Clock_out,
       not_1_out, t_ff_1_q, t_ff_1_qn, undriven;
  wire [3:0] decoder_1_opcode, decoder_1_operand1, decoder_1_operand2, decoder_1_operand3;
  wire [7:0] bus_control_1_bus_addr, decoder_1_immediate, multiplexer_2_out, PC_Control_pc_new, register_2_q;
  wire [15:0] alu_1_bus_out, n16_register_file_1_a, n16_register_file_1_b, register_1_q;

  Register #(.width(16)) register_1 (.D(alu_1_bus_out), .Q(register_1_q), .clk(and_1_out), .clr(Reset));  // open: en
  not not_1 (not_1_out, Clock_out);
  Clock Clock (.out(Clock_out));
  Decoder decoder_1 (
    .instruction(register_1_q), .opcode(decoder_1_opcode), .operand1(decoder_1_operand1),
    .operand2(decoder_1_operand2), .operand3(decoder_1_operand3), .immediate(decoder_1_immediate));
  T_Flip_Flop t_ff_1 (.clk(not_1_out), .T(1'b1), .Q(t_ff_1_q), .Qn(t_ff_1_qn), .reset(Reset));  // open: preset, en
  and and_1 (and_1_out, t_ff_1_qn, Clock_out);
  and and_2 (and_2_out, t_ff_1_q, Clock_out);
  ALU alu_1 (
    .a(n16_register_file_1_a), .b(n16_register_file_1_b), .op(decoder_1_opcode), .imm(decoder_1_immediate),
    .enable(bus_control_1_alu_enable), .bus_out(alu_1_bus_out));
  _16_register_file u_16_register_file_1 (
    .d(alu_1_bus_out), .Clk(bus_control_1_reg_write), .Rd(decoder_1_operand1), .Clr(Reset),
    .Ra(decoder_1_operand2), .Rb(decoder_1_operand3), .a(n16_register_file_1_a), .b(n16_register_file_1_b));
  PC_control PC_Control (
    .PC_new(PC_Control_pc_new), .op(decoder_1_opcode), .a(n16_register_file_1_a), .imm(decoder_1_immediate),
    .PC_old(register_2_q));
  Register register_2 (.D(PC_Control_pc_new), .Q(register_2_q), .clk(and_2_out), .clr(Reset));  // open: en
  Multiplexer #(.width(16), .enable("false")) multiplexer_1 (
    .in1(n16_register_file_1_a), .out(alu_1_bus_out), .sel(undriven));  // open: in0
  bus_control bus_control_1 (
    .a(n16_register_file_1_a), .reg_write(bus_control_1_reg_write), .ALU_enable(bus_control_1_alu_enable),
    .Read_Enabled(bus_control_1_read_enabled), .Display_Ready(bus_control_1_display_ready),
    .clock(Clock_out), .cycle(t_ff_1_q), .op(decoder_1_opcode), .imm(decoder_1_immediate),
    .bus_read(bus_control_1_bus_read), .bus_write(bus_control_1_bus_write), .bus_addr(bus_control_1_bus_addr));
  I_O i_o_1 (
    .Clock_In(Clock_out), .Display_Ready(bus_control_1_display_ready), .Reset_Out(Reset),
    .Display_Input(alu_1_bus_out), .Read_Ready(bus_control_1_read_enabled), .Keyboard_Out(alu_1_bus_out));
  Multiplexer #(.width(8), .enable("false")) multiplexer_2 (
    .in0(register_2_q), .in1(bus_control_1_bus_addr), .out(multiplexer_2_out), .sel(t_ff_1_q));
  RAM #(.dataWidth(16)) ram_1 (
    .addr(multiplexer_2_out), .data(alu_1_bus_out), .clk(bus_control_1_bus_write),
    .ld(bus_control_1_bus_read), .clr(in_1));  // open: sel

  // Notes on the sheet:
  //   Instruction
  //   Register
  //   Decoder
  //   Cycle
  //   Regs
  //   ALU
  //   Bus
  //   Control
  //   Program
  //   Counter
  //   Bus
endmodule

module four_register_file (
  input  [15:0] d,
  input  Ck,
  input  [1:0] Rd,
  input  Clr,
  input  [1:0] Ra,
  input  [1:0] Rb,
  output [15:0] a,
  output [15:0] b
);

  wire demultiplexer_1_out0, demultiplexer_1_out1, demultiplexer_1_out2, demultiplexer_1_out3;
  wire [15:0] register_1_q, register_2_q, register_3_q, register_4_q;

  Demultiplexer #(.select(2), .enable("false")) demultiplexer_1 (
    .out0(demultiplexer_1_out0), .out1(demultiplexer_1_out1), .out2(demultiplexer_1_out2),
    .out3(demultiplexer_1_out3), .in(Ck), .sel(Rd));
  Register #(.width(16)) register_1 (.D(d), .Q(register_1_q), .clk(demultiplexer_1_out0), .clr(Clr));  // open: en
  Register #(.width(16)) register_2 (.D(d), .Q(register_2_q), .clk(demultiplexer_1_out1), .clr(Clr));  // open: en
  Register #(.width(16)) register_3 (.D(d), .Q(register_3_q), .clk(demultiplexer_1_out2), .clr(Clr));  // open: en
  Register #(.width(16)) register_4 (.D(d), .Q(register_4_q), .clk(demultiplexer_1_out3), .clr(Clr));  // open: en
  Multiplexer #(.select(2), .width(16), .enable("false")) multiplexer_1 (
    .in0(register_1_q), .in1(register_2_q), .in2(register_3_q), .in3(register_4_q), .out(a), .sel(Ra));
  Multiplexer #(.select(2), .width(16), .enable("false")) multiplexer_2 (
    .in0(register_1_q), .in1(register_2_q), .in2(register_3_q), .in3(register_4_q), .out(b), .sel(Rb));
endmodule

module three_register_file (
  input  [15:0] d,
  input  Ck,
  input  [1:0] Rd,
  input  Clr,
  input  [1:0] Ra,
  input  [1:0] Rb,
  output [15:0] a,
  output [15:0] b
);

  wire demultiplexer_1_out1, demultiplexer_1_out2, demultiplexer_1_out3;
  wire [15:0] register_1_q, register_2_q, register_3_q;

  Demultiplexer #(.select(2), .enable("false")) demultiplexer_1 (
    .out1(demultiplexer_1_out1), .out2(demultiplexer_1_out2), .out3(demultiplexer_1_out3), .in(Ck), .sel(Rd));  // open: out0
  Register #(.width(16)) register_1 (.D(d), .Q(register_1_q), .clk(demultiplexer_1_out1), .clr(Clr));  // open: en
  Register #(.width(16)) register_2 (.D(d), .Q(register_2_q), .clk(demultiplexer_1_out2), .clr(Clr));  // open: en
  Register #(.width(16)) register_3 (.D(d), .Q(register_3_q), .clk(demultiplexer_1_out3), .clr(Clr));  // open: en
  Multiplexer #(.select(2), .width(16), .enable("false")) multiplexer_1 (
    .in0({16{1'b0}}), .in1(register_1_q), .in2(register_2_q), .in3(register_3_q), .out(a), .sel(Ra));
  Multiplexer #(.select(2), .width(16), .enable("false")) multiplexer_2 (
    .in0({16{1'b0}}), .in1(register_1_q), .in2(register_2_q), .in3(register_3_q), .out(b), .sel(Rb));
endmodule

module ALU (
  input  [15:0] a,
  input  [15:0] b,
  input  [3:0] op,
  input  [7:0] imm,
  input  enable,
  output [15:0] bus_out
);

  wire [15:0] adder_1_out, and_1_out, divider_1_out, multiplexer_1_out, multiplier_1_out, or_1_out, undriven,
       undriven_2;

  Adder #(.width(16)) adder_1 (.a(a), .b(b), .out(adder_1_out));  // open: cin, cout
  Multiplier #(.width(16)) multiplier_1 (.a(a), .b(b), .out(multiplier_1_out));  // open: cin, cout
  Divider #(.width(16)) divider_1 (.a(a), .b(b), .out(divider_1_out));  // open: upper, rem
  assign and_1_out = a & a & b;  // AND_Gate and_1, 16 bits wide
  assign or_1_out = a | b;  // OR_Gate or_1, 16 bits wide
  Multiplexer #(.select(3), .width(16), .enable("false")) multiplexer_1 (
    .in0(undriven_2), .in1(undriven), .in2(adder_1_out), .in3(multiplier_1_out), .in4(divider_1_out),
    .in5(and_1_out), .in6(or_1_out), .in7({{9{imm[7]}}, imm[6:0]}), .out(multiplexer_1_out), .sel(op[2:0]));
  assign bus_out = enable ? multiplexer_1_out : 16'bz;  // Controlled_Buffer controlled_buffer_1

  // Notes on the sheet:
  //   No More
  //   no More
  //   (sign extend)
endmodule

module PC_control (
  input  [15:0] a,
  input  [3:0] op,
  input  [7:0] imm,
  input  [7:0] PC_old,
  output [7:0] PC_new
);

  wire and_1_out, and_2_out, comparator_1_eq, comparator_1_gt, comparator_1_lt, multiplexer_1_out, not_1_out,
       not_2_out, not_3_out;
  wire [7:0] adder_1_out;

  Comparator #(.width(16)) comparator_1 (
    .a(a), .b({16{1'b0}}), .gt(comparator_1_gt), .eq(comparator_1_eq), .lt(comparator_1_lt));
  not not_1 (not_1_out, op[2]);
  and and_1 (and_1_out, op[3], not_1_out, multiplexer_1_out);
  Adder adder_1 (.a(8'h1), .b(PC_old), .out(adder_1_out));  // open: cin, cout
  not not_2 (not_2_out, comparator_1_eq);
  Multiplexer #(.select(2), .enable("false")) multiplexer_1 (
    .in0(comparator_1_eq), .in1(not_2_out), .in2(comparator_1_gt), .in3(comparator_1_lt),
    .out(multiplexer_1_out), .sel(op[1:0]));
  Multiplexer #(.width(8), .enable("false")) multiplexer_2 (
    .in0(adder_1_out), .in1(imm), .out(PC_new), .sel(and_1_out));
  not not_3 (not_3_out, and_2_out);
  and and_2 (and_2_out, op[3], op[2], op[1]);
  Multiplexer #(.width(16)) multiplexer_3 (.sel(op[0]), .en(not_3_out));  // open: in0, in1, out

  // Notes on the sheet:
  //   Perform conditional goto
  //   I/O
endmodule

module bus_control (
  input  [15:0] a,
  input  clock,
  input  cycle,
  input  [3:0] op,
  input  [7:0] imm,
  output reg_write,
  output ALU_enable,
  output Read_Enabled,
  output Display_Ready,
  output bus_read,
  output bus_write,
  output [7:0] bus_addr
);

  wire and_1_out, and_2_out, and_3_out, and_4_out, and_6_out, and_7_out, and_8_out, and_9_out, not_1_out,
       not_2_out, not_3_out, not_4_out, not_5_out, not_6_out, not_7_out, or_1_out, or_2_out;

  not not_1 (not_1_out, op[1]);
  not not_2 (not_2_out, op[3]);
  and and_1 (and_1_out, op[3], op[2], not_1_out);
  and and_2 (and_2_out, op[3], op[2], op[1]);
  and and_3 (and_3_out, clock, cycle);
  or or_1 (or_1_out, not_2_out, and_1_out);
  not not_3 (not_3_out, cycle);
  and and_4 (and_4_out, not_5_out, not_4_out);
  not not_4 (not_4_out, or_2_out);
  not not_5 (not_5_out, op[0]);
  or or_2 (or_2_out, op[1], op[2], op[3]);
  and and_5 (reg_write, and_6_out, not_7_out, Read_Enabled);
  and and_6 (and_6_out, or_1_out, and_3_out);
  and and_7 (and_7_out, not_2_out, cycle);
  or or_3 (bus_read, and_1_out, not_3_out);
  and and_8 (and_8_out, and_2_out, and_3_out);
  or or_4 (bus_write, and_8_out, and_4_out);
  Multiplexer #(.width(8), .enable("false")) multiplexer_1 (.in0(imm), .in1(a[7:0]), .out(bus_addr), .sel(and_9_out));
  and and_9 (and_9_out, op[0], or_2_out);
  not not_6 (not_6_out, or_2_out);
  and and_10 (ALU_enable, and_7_out, not_7_out, Read_Enabled);
  and and_11 (Display_Ready, op[0], not_6_out);
  not not_7 (not_7_out, Display_Ready);

  // Notes on the sheet:
  //   Implements Load/Store in the CPU
endmodule

module Decoder (
  input  [15:0] instruction,
  output [3:0] opcode,
  output [3:0] operand1,
  output [3:0] operand2,
  output [3:0] operand3,
  output [7:0] immediate
);

  Multiplexer #(.width(4), .enable("false")) multiplexer_1 (
    .in0(instruction[7:4]), .in1(instruction[11:8]), .out(operand2), .sel(instruction[15]));

  assign immediate = instruction[7:0];
  assign opcode = instruction[15:12];
  assign operand1 = instruction[11:8];
  assign operand3 = instruction[3:0];

  // Notes on the sheet:
  //   The MUX copies operand1 to operand2 for program and bus control
endmodule

module Hex_to_Display (
  input  [3:0] INPUT,
  output [7:0] Output
);

  Multiplexer #(.select(4), .enable("false")) multiplexer_1 (
    .in0(1'b1), .in1(1'b0), .in2(1'b1), .in3(1'b1), .in4(1'b0), .in5(1'b1), .in6(1'b1), .in7(1'b1),
    .in8(1'b1), .in9(1'b1), .out(Output[6]), .sel(INPUT));  // open: in10, in11, in12, in13, in14, in15
  Multiplexer #(.select(4), .enable("false")) multiplexer_2 (
    .in0(1'b1), .in1(1'b1), .in2(1'b1), .in3(1'b1), .in4(1'b1), .in5(1'b0), .in6(1'b0), .in7(1'b1),
    .in8(1'b1), .in9(1'b1), .out(Output[7]), .sel(INPUT));  // open: in10, in11, in12, in13, in14, in15
  Multiplexer #(.select(4), .enable("false")) multiplexer_3 (
    .in0(1'b1), .in1(1'b1), .in2(1'b0), .in3(1'b1), .in4(1'b1), .in5(1'b1), .in6(1'b1), .in7(1'b1),
    .in8(1'b1), .in9(1'b1), .out(Output[1]), .sel(INPUT));  // open: in10, in11, in12, in13, in14, in15
  Multiplexer #(.select(4), .enable("false")) multiplexer_4 (
    .in0(1'b1), .in1(1'b0), .in2(1'b1), .in3(1'b1), .in4(1'b0), .in5(1'b1), .in6(1'b1), .in7(1'b0),
    .in8(1'b1), .in9(1'b1), .out(Output[2]), .sel(INPUT));  // open: in10, in11, in12, in13, in14, in15
  Multiplexer #(.select(4), .enable("false")) multiplexer_5 (
    .in0(1'b1), .in1(1'b0), .in2(1'b1), .in3(1'b0), .in4(1'b0), .in5(1'b0), .in6(1'b1), .in7(1'b0),
    .in8(1'b1), .in9(1'b0), .out(Output[3]), .sel(INPUT));  // open: in10, in11, in12, in13, in14, in15
  Multiplexer #(.select(4), .enable("false")) multiplexer_6 (
    .in0(1'b1), .in1(1'b0), .in2(1'b0), .in3(1'b0), .in4(1'b1), .in5(1'b1), .in6(1'b1), .in7(1'b0),
    .in8(1'b1), .in9(1'b1), .out(Output[5]), .sel(INPUT));  // open: in10, in11, in12, in13, in14, in15
  Multiplexer #(.select(4), .enable("false")) multiplexer_7 (
    .in0(1'b0), .in1(1'b0), .in2(1'b1), .in3(1'b1), .in4(1'b1), .in5(1'b1), .in6(1'b1), .in7(1'b0),
    .in8(1'b1), .in9(1'b1), .out(Output[4]), .sel(INPUT));  // open: in10, in11, in12, in13, in14, in15

  // Notes on the sheet:
  //   A
  //   B
  //   C
  //   D
  //   E
  //   F
  //   G
endmodule

module Decimal_Places (
  input  [15:0] Input,
  output [3:0] _10_000,
  output [3:0] _1_000,
  output [3:0] _100,
  output [3:0] _10,
  output [3:0] _1
);

  wire [3:0] divider_1_out, divider_1_out_2, divider_2_out, divider_2_out_2, divider_2_out_3, divider_3_out,
       divider_3_out_2, divider_3_out_3, divider_4_out, divider_4_out_2, divider_4_out_3, divider_4_rem,
       divider_4_rem_2, divider_4_rem_3;
  wire [15:0] divider_1_rem, divider_2_rem, divider_3_rem;
  wire [15:12] divider_1_out_3;

  Divider #(.width(16)) divider_1 (
    .a(Input), .b(16'h2710), .out({divider_1_out_3, divider_1_out_2, divider_1_out, _10_000}),
    .rem(divider_1_rem));  // open: upper
  Divider #(.width(16)) divider_2 (
    .a(divider_1_rem), .b(16'h3e8), .out({divider_2_out_3, divider_2_out_2, divider_2_out, _1_000}),
    .rem(divider_2_rem));  // open: upper
  Divider #(.width(16)) divider_3 (
    .a(divider_2_rem), .b(16'h64), .out({divider_3_out_3, divider_3_out_2, divider_3_out, _100}),
    .rem(divider_3_rem));  // open: upper
  Divider #(.width(16)) divider_4 (
    .a(divider_3_rem), .b(16'ha), .out({divider_4_out_3, divider_4_out_2, divider_4_out, _10}),
    .rem({divider_4_rem_3, divider_4_rem_2, divider_4_rem, _1}));  // open: upper
endmodule

module I_O (
  input  Clock_In,
  input  Display_Ready,
  input  Reset_Out,
  input  [15:0] Display_Input,
  output Read_Ready,
  output [15:0] Keyboard_Out
);

  wire and_1_out, button_2_out, button_3_out, keyboard_1_avail;
  wire [3:0] decimal_places_1__1, decimal_places_1__1_000, decimal_places_1__10, decimal_places_1__10_000,
       decimal_places_1__100;
  wire [6:0] keyboard_1_data;
  wire [7:0] hex_to_display_1_output, hex_to_display_2_output, hex_to_display_3_output,
       hex_to_display_4_output, hex_to_display_5_output;
  wire [15:0] multiplexer_1_out, register_1_q;

  Register #(.width(16)) register_1 (.D(Display_Input), .Q(register_1_q), .clk(Display_Ready));  // open: en, clr
  Multiplexer #(.width(16), .enable("false")) multiplexer_1 (
    .in0(register_1_q), .in1(Display_Input), .out(multiplexer_1_out), .sel(Display_Ready));
  _7_Segment_Display u_7_segment_display_1 (
    .g(hex_to_display_1_output[4]), .f(hex_to_display_1_output[5]), .a(hex_to_display_1_output[6]),
    .b(hex_to_display_1_output[7]), .e(hex_to_display_1_output[3]), .d(hex_to_display_1_output[2]),
    .c(hex_to_display_1_output[1]), .dp(hex_to_display_1_output[0]));
  Hex_to_Display hex_to_display_1 (.INPUT(decimal_places_1__10_000), .Output(hex_to_display_1_output));
  Keyboard keyboard_1 (
    .clk(Clock_In), .re(and_1_out), .clr(button_2_out), .avail(keyboard_1_avail), .data(keyboard_1_data));
  Button button_1 (.out(Reset_Out));
  _7_Segment_Display u_7_segment_display_2 (
    .g(hex_to_display_2_output[4]), .f(hex_to_display_2_output[5]), .a(hex_to_display_2_output[6]),
    .b(hex_to_display_2_output[7]), .e(hex_to_display_2_output[3]), .d(hex_to_display_2_output[2]),
    .c(hex_to_display_2_output[1]), .dp(hex_to_display_2_output[0]));
  Hex_to_Display hex_to_display_2 (.INPUT(decimal_places_1__1_000), .Output(hex_to_display_2_output));
  Decimal_Places decimal_places_1 (
    .Input(multiplexer_1_out), ._10_000(decimal_places_1__10_000), ._1_000(decimal_places_1__1_000),
    ._100(decimal_places_1__100), ._10(decimal_places_1__10), ._1(decimal_places_1__1));
  and and_1 (and_1_out, keyboard_1_avail, button_3_out);
  Button button_2 (.out(button_2_out));
  _7_Segment_Display u_7_segment_display_3 (
    .g(hex_to_display_3_output[4]), .f(hex_to_display_3_output[5]), .a(hex_to_display_3_output[6]),
    .b(hex_to_display_3_output[7]), .e(hex_to_display_3_output[3]), .d(hex_to_display_3_output[2]),
    .c(hex_to_display_3_output[1]), .dp(hex_to_display_3_output[0]));
  Hex_to_Display hex_to_display_3 (.INPUT(decimal_places_1__100), .Output(hex_to_display_3_output));
  Button button_3 (.out(button_3_out));
  _7_Segment_Display u_7_segment_display_4 (
    .g(hex_to_display_4_output[4]), .f(hex_to_display_4_output[5]), .a(hex_to_display_4_output[6]),
    .b(hex_to_display_4_output[7]), .e(hex_to_display_4_output[3]), .d(hex_to_display_4_output[2]),
    .c(hex_to_display_4_output[1]), .dp(hex_to_display_4_output[0]));
  Hex_to_Display hex_to_display_4 (.INPUT(decimal_places_1__10), .Output(hex_to_display_4_output));
  Keyboard_to_Number keyboard_to_number_1 (
    .Clear(and_1_out), .Clock(Clock_In), .in_3(keyboard_1_data), .Number_Ready(Read_Ready),
    .out_5(Keyboard_Out));
  _7_Segment_Display u_7_segment_display_5 (
    .g(hex_to_display_5_output[4]), .f(hex_to_display_5_output[5]), .a(hex_to_display_5_output[6]),
    .b(hex_to_display_5_output[7]), .e(hex_to_display_5_output[3]), .d(hex_to_display_5_output[2]),
    .c(hex_to_display_5_output[1]), .dp(hex_to_display_5_output[0]));
  Hex_to_Display hex_to_display_5 (.INPUT(decimal_places_1__1), .Output(hex_to_display_5_output));

  // Notes on the sheet:
  //   Reset CPU
  //   --------DISPLAY--------
  //   Clear
  //   Send
  //   (Hold)
endmodule

module Keyboard_to_Number (
  input  Clear,
  input  Clock,
  input  [6:0] in_3,
  output Number_Ready,
  output [15:0] out_5
);

  wire and_1_out, comparator_1_eq;
  wire [2:0] counter_1_q;
  wire [6:0] subtractor_1_out;
  wire [15:0] adder_1_out, multiplexer_1_out, multiplier_1_out, register_1_q;

  Comparator #(.width(3)) comparator_1 (.a(counter_1_q), .b(3'b111), .eq(comparator_1_eq));  // open: gt, lt
  and and_1 (and_1_out, Clear, comparator_1_eq);
  Counter #(.width(3), .max('h7), .ongoal("stay")) counter_1 (
    .Q(counter_1_q), .clk(Clock), .clr(and_1_out));  // open: load, D, count, carry
  Subtractor #(.width(7)) subtractor_1 (.a(in_3), .b(7'b0110000), .out(subtractor_1_out));  // open: bin, bout
  Multiplexer #(.select(3), .width(16), .enable("false")) multiplexer_1 (
    .in0(16'h2710), .in1(16'h3e8), .in2(16'h64), .in3(16'ha), .in4(16'h1), .out(multiplexer_1_out),
    .sel(counter_1_q));  // open: in5, in6, in7
  Multiplier #(.width(16)) multiplier_1 (
    .a({{9{1'b0}}, subtractor_1_out}), .b(multiplexer_1_out), .out(multiplier_1_out));  // open: cin, cout
  Comparator #(.width(3)) comparator_2 (.a(counter_1_q), .b(3'b101), .eq(Number_Ready));  // open: gt, lt
  Adder #(.width(16)) adder_1 (.a(multiplier_1_out), .b(register_1_q), .out(adder_1_out));  // open: cin, cout
  Register #(.width(16), .trigger("falling")) register_1 (
    .D(out_5), .Q(register_1_q), .clk(Clock), .clr(and_1_out));  // open: en
  Register #(.width(16)) Total (.D(adder_1_out), .Q(out_5), .clk(Clock), .clr(and_1_out));  // open: en
endmodule
